// Logisim project ex2.circ as structural Verilog: 1 circuit, main circuit compute_BrUn
module compute_BrUn (
  input  [31:0] INSTRUCTION,
  output BrUn
);

  wire B_type, bgeu, bltu, comparator_2_eq, comparator_3_eq;

  // Probe on 7'b1100011
  Comparator #(.mode("unsigned"), .width(7)) comparator_1 (
    .a(INSTRUCTION[6:0]), .b(7'b1100011), .eq(B_type));  // open: gt, lt
  Comparator #(.mode("unsigned"), .width(3)) comparator_2 (
    .a(INSTRUCTION[14:12]), .b(3'b111), .eq(comparator_2_eq));  // open: gt, lt
  Comparator #(.mode("unsigned"), .width(3)) comparator_3 (
    .a(INSTRUCTION[14:12]), .b(3'b110), .eq(comparator_3_eq));  // open: gt, lt
  or or_1 (BrUn, bgeu, bltu);
  and and_1 (bgeu, B_type, comparator_2_eq);
  and and_2 (bltu, B_type, comparator_3_eq);

  // Other names for the same wires on the sheet: Opcode[6:0] = INSTRUCTION[6:0]; Funct3[2:0] = INSTRUCTION[14:12];
  //   Funct7[6:0] = INSTRUCTION[31:25]
endmodule
