// Logisim project control-logic.circ as structural Verilog: 1 circuit, main circuit control_logic
module control_logic (
  input  [31:0] Instruction,
  input  BrEq,
  input  BrLt,
  output PCSel,
  output RegWEn,
  output [2:0] ImmSel,
  output BrUn,
  output ASel,
  output BSel,
  output [3:0] ALUSel,
  output MemWEn,
  output [1:0] WBSel
);

  wire add, addi, and_11_out, and_12_out, and_13_out, and_14_out, and_15_out, and_16_out, and_R, andi, auipc,
       B_type, beq, bge, bgeu, blt, bltu, bne, comparator_1_eq, comparator_2_eq, comparator_11_eq,
       comparator_12_eq, comparator_13_eq, comparator_14_eq, comparator_15_eq, comparator_16_eq,
       comparator_17_eq, comparator_18_eq, comparator_19_eq, comparator_20_eq, comparator_21_eq,
       comparator_22_eq, comparator_23_eq, comparator_24_eq, comparator_25_eq, comparator_26_eq,
       comparator_27_eq, comparator_28_eq, comparator_29_eq, comparator_30_eq, comparator_31_eq,
       comparator_32_eq, comparator_33_eq, comparator_34_eq, comparator_35_eq, comparator_36_eq,
       comparator_37_eq, comparator_38_eq, comparator_39_eq, comparator_40_eq, comparator_41_eq,
       comparator_42_eq, comparator_43_eq, comparator_44_eq, comparator_45_eq, comparator_46_eq,
       comparator_47_eq, comparator_48_eq, comparator_49_eq, comparator_50_eq, comparator_51_eq,
       comparator_52_eq, comparator_53_eq, comparator_54_eq, comparator_55_eq, comparator_56_eq,
       comparator_57_eq, jal, jalr, lb, lh, Load_type, lui, lw, mul, mulh, mulhu, not_1_out, not_2_out,
       not_3_out, or_1_out, or_2_out, or_3_out, or_4_out, or_R, ori, R_type, Regular_I_type, sb, sh, sll_R,
       slli, slt, slti, sra_R, srai, srl_R, srli, Store_type, sub, sw, xor_R, xori;
  wire [5:0] InstructionSel;
  wire [15:14] rom_1_data;

  ROM #(.addrWidth(6), .dataWidth(16)) rom_1 (
    .addr(InstructionSel), .data({rom_1_data, WBSel, MemWEn, ALUSel, BSel, ASel, BrUn, ImmSel, RegWEn}));
  // Probe on 7'b1101111
  // Probe on 7'b1100111
  // Probe on 3'b000
  Priority_Encoder #(.select_enc(6)) priority_encoder_1 (
    .in0(addi), .in1(andi), .in2(ori), .in3(xori), .in4(slli), .in5(srli), .in6(srai), .in7(slti), .in8(add),
    .in9(sub), .in10(and_R), .in11(or_R), .in12(xor_R), .in13(sll_R), .in14(srl_R), .in15(sra_R), .in16(slt),
    .in17(mul), .in18(mulh), .in19(mulhu), .in20(beq), .in21(bge), .in22(bgeu), .in23(blt), .in24(bltu),
    .in25(bne), .in26(lb), .in27(lh), .in28(lw), .in29(sb), .in30(sh), .in31(sw), .in32(jal), .in33(jalr),
    .in34(auipc), .in35(lui), .out(InstructionSel));  // open: in36, in37, in38, in39, in40, in41, in42, in43, in44, in45, in46, in47, in48, in49, in50, in51, in52, in53, in54, in55, in56, in57, in58, in59, in60, in61, in62, in63, gs, en_out, en_in
  // Probe on 7'b0110111
  // Probe on 7'b0010111
  Comparator #(.mode("unsigned"), .width(7)) comparator_1 (
    .a(Instruction[6:0]), .b(7'b1100111), .eq(comparator_1_eq));  // open: gt, lt
  Comparator #(.mode("unsigned"), .width(3)) comparator_2 (
    .a(Instruction[14:12]), .b(3'b000), .eq(comparator_2_eq));  // open: gt, lt
  // Probe on ImmSel
  // Probe on RegWEn
  // Probe on InstructionSel
  Comparator #(.mode("unsigned"), .width(7)) comparator_3 (
    .a(Instruction[6:0]), .b(7'b0110111), .eq(lui));  // open: gt, lt
  Comparator #(.mode("unsigned"), .width(7)) comparator_4 (
    .a(Instruction[6:0]), .b(7'b0010111), .eq(auipc));  // open: gt, lt
  Comparator #(.mode("unsigned"), .width(7)) comparator_5 (
    .a(Instruction[6:0]), .b(7'b1101111), .eq(jal));  // open: gt, lt
  and and_1 (jalr, comparator_1_eq, comparator_2_eq);
  // Probe on ASel
  // Probe on BSel
  // Probe on BrUn
  // Probe on ALUSel
  // Probe on MemWEn
  // Probe on WBSel
  // Probe on 7'b0010011
  // Probe on 7'b0110011
  // Probe on 7'b1100011
  // Probe on 7'b0000011
  // Probe on 7'b0100011
  Comparator #(.mode("unsigned"), .width(7)) comparator_6 (
    .a(Instruction[6:0]), .b(7'b0010011), .eq(Regular_I_type));  // open: gt, lt
  Comparator #(.mode("unsigned"), .width(7)) comparator_7 (
    .a(Instruction[6:0]), .b(7'b0110011), .eq(R_type));  // open: gt, lt
  Comparator #(.mode("unsigned"), .width(7)) comparator_8 (
    .a(Instruction[6:0]), .b(7'b1100011), .eq(B_type));  // open: gt, lt
  Comparator #(.mode("unsigned"), .width(7)) comparator_9 (
    .a(Instruction[6:0]), .b(7'b0000011), .eq(Load_type));  // open: gt, lt
  Comparator #(.mode("unsigned"), .width(7)) comparator_10 (
    .a(Instruction[6:0]), .b(7'b0100011), .eq(Store_type));  // open: gt, lt
  Comparator #(.mode("unsigned"), .width(3)) comparator_11 (
    .a(Instruction[14:12]), .b(3'b101), .eq(comparator_11_eq));  // open: gt, lt
  Comparator #(.mode("unsigned"), .width(7)) comparator_12 (
    .a({7{1'b0}}), .b(Instruction[31:25]), .eq(comparator_12_eq));  // open: gt, lt
  Comparator #(.mode("unsigned"), .width(3)) comparator_13 (
    .a(Instruction[14:12]), .b(3'b101), .eq(comparator_13_eq));  // open: gt, lt
  Comparator #(.mode("unsigned"), .width(7)) comparator_14 (
    .a(7'b0100000), .b(Instruction[31:25]), .eq(comparator_14_eq));  // open: gt, lt
  Comparator #(.mode("unsigned"), .width(3)) comparator_15 (
    .a(Instruction[14:12]), .b(3'b000), .eq(comparator_15_eq));  // open: gt, lt
  Comparator #(.mode("unsigned"), .width(3)) comparator_16 (
    .a(Instruction[14:12]), .b(3'b111), .eq(comparator_16_eq));  // open: gt, lt
  Comparator #(.mode("unsigned"), .width(3)) comparator_17 (
    .a(Instruction[14:12]), .b(3'b111), .eq(comparator_17_eq));  // open: gt, lt
  Comparator #(.mode("unsigned"), .width(3)) comparator_18 (
    .a(Instruction[14:12]), .b(3'b110), .eq(comparator_18_eq));  // open: gt, lt
  Comparator #(.mode("unsigned"), .width(3)) comparator_19 (
    .a(Instruction[14:12]), .b(3'b100), .eq(comparator_19_eq));  // open: gt, lt
  Comparator #(.mode("unsigned"), .width(3)) comparator_20 (
    .a(Instruction[14:12]), .b(3'b001), .eq(comparator_20_eq));  // open: gt, lt
  Comparator #(.mode("unsigned"), .width(3)) comparator_21 (
    .a(Instruction[14:12]), .b(3'b010), .eq(comparator_21_eq));  // open: gt, lt
  and and_2 (addi, Regular_I_type, comparator_15_eq);
  and and_3 (andi, Regular_I_type, comparator_16_eq);
  and and_4 (andi, Regular_I_type, comparator_17_eq);
  and and_5 (ori, Regular_I_type, comparator_18_eq);
  and and_6 (xori, Regular_I_type, comparator_19_eq);
  and and_7 (slli, Regular_I_type, comparator_20_eq);
  and and_8 (srli, Regular_I_type, comparator_11_eq, comparator_12_eq);
  and and_9 (slti, Regular_I_type, comparator_21_eq);
  and and_10 (srai, Regular_I_type, comparator_13_eq, comparator_14_eq);
  not not_1 (not_1_out, BrLt);
  not not_2 (not_2_out, BrLt);
  Comparator #(.mode("unsigned"), .width(3)) comparator_22 (
    .a(Instruction[14:12]), .b(3'b000), .eq(comparator_22_eq));  // open: gt, lt
  Comparator #(.mode("unsigned"), .width(7)) comparator_23 (
    .a({7{1'b0}}), .b(Instruction[31:25]), .eq(comparator_23_eq));  // open: gt, lt
  Comparator #(.mode("unsigned"), .width(3)) comparator_24 (
    .a(Instruction[14:12]), .b(3'b000), .eq(comparator_24_eq));  // open: gt, lt
  Comparator #(.mode("unsigned"), .width(7)) comparator_25 (
    .a(7'b0100000), .b(Instruction[31:25]), .eq(comparator_25_eq));  // open: gt, lt
  Comparator #(.mode("unsigned"), .width(3)) comparator_26 (
    .a(Instruction[14:12]), .b(3'b111), .eq(comparator_26_eq));  // open: gt, lt
  Comparator #(.mode("unsigned"), .width(7)) comparator_27 (
    .a({7{1'b0}}), .b(Instruction[31:25]), .eq(comparator_27_eq));  // open: gt, lt
  Comparator #(.mode("unsigned"), .width(3)) comparator_28 (
    .a(Instruction[14:12]), .b(3'b110), .eq(comparator_28_eq));  // open: gt, lt
  Comparator #(.mode("unsigned"), .width(7)) comparator_29 (
    .a({7{1'b0}}), .b(Instruction[31:25]), .eq(comparator_29_eq));  // open: gt, lt
  Comparator #(.mode("unsigned"), .width(3)) comparator_30 (
    .a(Instruction[14:12]), .b(3'b100), .eq(comparator_30_eq));  // open: gt, lt
  Comparator #(.mode("unsigned"), .width(7)) comparator_31 (
    .a({7{1'b0}}), .b(Instruction[31:25]), .eq(comparator_31_eq));  // open: gt, lt
  Comparator #(.mode("unsigned"), .width(3)) comparator_32 (
    .a(Instruction[14:12]), .b(3'b001), .eq(comparator_32_eq));  // open: gt, lt
  Comparator #(.mode("unsigned"), .width(7)) comparator_33 (
    .a({7{1'b0}}), .b(Instruction[31:25]), .eq(comparator_33_eq));  // open: gt, lt
  Comparator #(.mode("unsigned"), .width(3)) comparator_34 (
    .a(Instruction[14:12]), .b(3'b101), .eq(comparator_34_eq));  // open: gt, lt
  Comparator #(.mode("unsigned"), .width(7)) comparator_35 (
    .a({7{1'b0}}), .b(Instruction[31:25]), .eq(comparator_35_eq));  // open: gt, lt
  Comparator #(.mode("unsigned"), .width(3)) comparator_36 (
    .a(Instruction[14:12]), .b(3'b101), .eq(comparator_36_eq));  // open: gt, lt
  Comparator #(.mode("unsigned"), .width(7)) comparator_37 (
    .a(7'b0100000), .b(Instruction[31:25]), .eq(comparator_37_eq));  // open: gt, lt
  Comparator #(.mode("unsigned"), .width(3)) comparator_38 (
    .a(Instruction[14:12]), .b(3'b010), .eq(comparator_38_eq));  // open: gt, lt
  Comparator #(.mode("unsigned"), .width(7)) comparator_39 (
    .a({7{1'b0}}), .b(Instruction[31:25]), .eq(comparator_39_eq));  // open: gt, lt
  Comparator #(.mode("unsigned"), .width(3)) comparator_40 (
    .a(Instruction[14:12]), .b(3'b000), .eq(comparator_40_eq));  // open: gt, lt
  Comparator #(.mode("unsigned"), .width(7)) comparator_41 (
    .a(7'b0000001), .b(Instruction[31:25]), .eq(comparator_41_eq));  // open: gt, lt
  Comparator #(.mode("unsigned"), .width(3)) comparator_42 (
    .a(Instruction[14:12]), .b(3'b001), .eq(comparator_42_eq));  // open: gt, lt
  Comparator #(.mode("unsigned"), .width(7)) comparator_43 (
    .a(7'b0000001), .b(Instruction[31:25]), .eq(comparator_43_eq));  // open: gt, lt
  Comparator #(.mode("unsigned"), .width(3)) comparator_44 (
    .a(Instruction[14:12]), .b(3'b011), .eq(comparator_44_eq));  // open: gt, lt
  Comparator #(.mode("unsigned"), .width(7)) comparator_45 (
    .a(7'b0000001), .b(Instruction[31:25]), .eq(comparator_45_eq));  // open: gt, lt
  or or_1 (or_1_out, BrEq, not_1_out);
  or or_2 (or_2_out, BrEq, not_2_out);
  not not_3 (not_3_out, BrEq);
  and and_11 (and_11_out, beq, BrEq);
  and and_12 (and_12_out, bge, or_1_out);
  and and_13 (and_13_out, bgeu, or_2_out);
  and and_14 (and_14_out, blt, BrLt);
  and and_15 (and_15_out, bltu, BrLt);
  and and_16 (and_16_out, bne, not_3_out);
  and and_17 (add, R_type, comparator_22_eq, comparator_23_eq);
  and and_18 (sub, R_type, comparator_24_eq, comparator_25_eq);
  and and_19 (and_R, R_type, comparator_26_eq, comparator_27_eq);
  and and_20 (or_R, R_type, comparator_28_eq, comparator_29_eq);
  and and_21 (xor_R, R_type, comparator_30_eq, comparator_31_eq);
  and and_22 (sll_R, R_type, comparator_32_eq, comparator_33_eq);
  and and_23 (srl_R, R_type, comparator_34_eq, comparator_35_eq);
  and and_24 (sra_R, R_type, comparator_36_eq, comparator_37_eq);
  and and_25 (slt, R_type, comparator_38_eq, comparator_39_eq);
  and and_26 (mul, R_type, comparator_40_eq, comparator_41_eq);
  and and_27 (mulh, R_type, comparator_42_eq, comparator_43_eq);
  and and_28 (mulhu, R_type, comparator_44_eq, comparator_45_eq);
  or or_3 (or_3_out, and_11_out, and_12_out, and_13_out, and_14_out, and_15_out, and_16_out);
  or or_4 (or_4_out, jal, jalr);
  or or_5 (PCSel, or_3_out, or_4_out);
  Comparator #(.mode("unsigned"), .width(3)) comparator_46 (
    .a(Instruction[14:12]), .b(3'b000), .eq(comparator_46_eq));  // open: gt, lt
  Comparator #(.mode("unsigned"), .width(3)) comparator_47 (
    .a(Instruction[14:12]), .b(3'b101), .eq(comparator_47_eq));  // open: gt, lt
  Comparator #(.mode("unsigned"), .width(3)) comparator_48 (
    .a(Instruction[14:12]), .b(3'b111), .eq(comparator_48_eq));  // open: gt, lt
  Comparator #(.mode("unsigned"), .width(3)) comparator_49 (
    .a(Instruction[14:12]), .b(3'b100), .eq(comparator_49_eq));  // open: gt, lt
  Comparator #(.mode("unsigned"), .width(3)) comparator_50 (
    .a(Instruction[14:12]), .b(3'b110), .eq(comparator_50_eq));  // open: gt, lt
  Comparator #(.mode("unsigned"), .width(3)) comparator_51 (
    .a(Instruction[14:12]), .b(3'b001), .eq(comparator_51_eq));  // open: gt, lt
  and and_29 (beq, B_type, comparator_46_eq);
  and and_30 (bge, B_type, comparator_47_eq);
  and and_31 (bgeu, B_type, comparator_48_eq);
  and and_32 (blt, B_type, comparator_49_eq);
  and and_33 (bltu, B_type, comparator_50_eq);
  and and_34 (bne, B_type, comparator_51_eq);
  or or_6 (BrUn, bgeu, bltu);
  Comparator #(.mode("unsigned"), .width(3)) comparator_52 (
    .a(Instruction[14:12]), .b(3'b000), .eq(comparator_52_eq));  // open: gt, lt
  Comparator #(.mode("unsigned"), .width(3)) comparator_53 (
    .a(Instruction[14:12]), .b(3'b001), .eq(comparator_53_eq));  // open: gt, lt
  and and_35 (lb, Load_type, comparator_52_eq);
  Comparator #(.mode("unsigned"), .width(3)) comparator_54 (
    .a(Instruction[14:12]), .b(3'b010), .eq(comparator_54_eq));  // open: gt, lt
  Comparator #(.mode("unsigned"), .width(3)) comparator_55 (
    .a(Instruction[14:12]), .b(3'b000), .eq(comparator_55_eq));  // open: gt, lt
  Comparator #(.mode("unsigned"), .width(3)) comparator_56 (
    .a(Instruction[14:12]), .b(3'b001), .eq(comparator_56_eq));  // open: gt, lt
  Comparator #(.mode("unsigned"), .width(3)) comparator_57 (
    .a(Instruction[14:12]), .b(3'b010), .eq(comparator_57_eq));  // open: gt, lt
  and and_36 (lh, Load_type, comparator_53_eq);
  and and_37 (lw, Load_type, comparator_54_eq);
  and and_38 (sb, Store_type, comparator_55_eq);
  and and_39 (sh, Store_type, comparator_56_eq);
  and and_40 (sw, Store_type, comparator_57_eq);

  // Other names for the same wires on the sheet: Opcode[6:0] = Instruction[6:0]; Funct3[2:0] = Instruction[14:12];
  //   Funct7[6:0] = Instruction[31:25]

  // Notes on the sheet:
  //   INPUTS to your circuit
  //   Connect ROM Input here ->
  //   contents of rom_1 (hex, n*v repeats v):
  //   1041 13c1 1341 1241 10c1 12c1 16c1 1141 1001 1601 1381 1301 1201 1081 1281 1681 1101 1401 1481 1581
  //   1064 1064 1074 1064 1074 1064 41 41 41 842 842 842 2069 2041 1067 17c7
  //   ROM FOR CONTROL LOGIC
  //   DON'T CHANGE THE LOCATIONS OF THE INPUTS AND OUTPUTS!
  //   This is only if you choose to do the ROM option
  //   OUTPUT from your circuit
  //   Reminder: If using ROM, use combinational logic for PCSel
  //   for I and R type instruction test
endmodule
