// Logisim project cpu.circ as structural Verilog: 1 circuit, main circuit cpu
module cpu (
  input  clk,
  input  [31:0] Instruction,
  input  [31:0] MemReadData,
  output [31:0] MemAddress,
  output [31:0] ProgramCounter,
  output [31:0] ra,
  output [31:0] sp,
  output [31:0] t0,
  output [31:0] t1,
  output [31:0] t2,
  output [31:0] s0,
  output [31:0] s1,
  output [31:0] a0,
  output [3:0] MemWriteMask,
  output [31:0] MemWriteData
);

  wire ASel, BrEq, BrLt, BrUn, BSel, MemWEn, PCSel, RegWEn;
  wire [1:0] WBSel;
  wire [2:0] ImmSel;
  wire [3:0] ALUSel;
  wire [31:0] adder_1_out, DataToReg, Immediate, Instruction_p, multiplexer_1_out, multiplexer_2_out,
       multiplexer_3_out, multiplexer_4_out, PCAdd4, ProgramCounter_p, ReadData1, ReadData2, WBRegData;

  // Probe on Instruction_p
  Register #(.width(32)) register_1 (.D(multiplexer_1_out), .clk(clk), .Q(Instruction_p));  // open: en, clr
  Multiplexer #(.width(32)) multiplexer_1 (.in0(Instruction), .in1(32'h13), .out(multiplexer_1_out), .sel(PCSel));
  // Probe on Instruction_p[11:7]
  // Probe on Instruction_p[24:20]
  // Probe on Instruction_p[19:15]
  // Probe on MemAddress
  Adder #(.width(32)) adder_1 (.a(ProgramCounter), .b(32'h4), .out(adder_1_out));  // open: cin, cout
  // Probe on WBRegData
  // Probe on clk
  Register #(.width(32)) PC (.D(multiplexer_2_out), .clk(clk), .Q(ProgramCounter));  // open: en, clr
  Multiplexer #(.width(32)) multiplexer_2 (.in0(adder_1_out), .in1(MemAddress), .out(multiplexer_2_out), .sel(PCSel));
  // Probe on ProgramCounter
  // Probe on ra
  // Probe on ImmSel
  // Probe on sp
  Register #(.width(32)) register_2 (.D(ProgramCounter), .clk(clk), .Q(ProgramCounter_p));  // open: en, clr
  // Probe on BrLt
  // Probe on BrEq
  // Probe on ImmSel
  // Probe on RegWEn
  // Probe on PCSel
  // Probe on t0
  // Probe on ProgramCounter_p
  regfile regfile_1 (
    .ReadIndex1(Instruction_p[19:15]), .ReadIndex2(Instruction_p[24:20]), .WriteIndex(Instruction_p[11:7]),
    .WriteData(WBRegData), .RegWEn(RegWEn), .clk(clk), .ra(ra), .sp(sp), .t0(t0), .t1(t1), .t2(t2), .s0(s0),
    .s1(s1), .a0(a0), .ReadData1(ReadData1), .ReadData2(ReadData2));
  // Probe on ReadData1
  // Probe on t1
  imm_gen imm_gen_1 (.Instruction(Instruction_p), .ImmSel(ImmSel), .Immediate(Immediate));
  // Probe on Immediate
  Adder #(.width(32)) adder_2 (.a(ProgramCounter_p), .b(32'h4), .out(PCAdd4));  // open: cin, cout
  // Probe on ReadData2
  control_logic control_logic_1 (
    .PCSel(PCSel), .RegWEn(RegWEn), .ImmSel(ImmSel), .BrUn(BrUn), .ASel(ASel), .BSel(BSel), .ALUSel(ALUSel),
    .MemWEn(MemWEn), .WBSel(WBSel), .Instruction(Instruction_p), .BrEq(BrEq), .BrLt(BrLt));
  // Probe on t2
  // Probe on s0
  // Probe on s1
  Multiplexer #(.width(32)) multiplexer_3 (
    .in0(ReadData1), .in1(ProgramCounter_p), .out(multiplexer_3_out), .sel(ASel));
  Multiplexer #(.width(32)) multiplexer_4 (.in0(ReadData2), .in1(Immediate), .out(multiplexer_4_out), .sel(BSel));
  // Probe on a0
  alu alu_1 (.ALUResult(MemAddress), .A(multiplexer_3_out), .B(multiplexer_4_out), .ALUSel(ALUSel));
  // Probe on MemAddress
  branch_comp branch_comp_1 (.BrData1(ReadData1), .BrData2(ReadData2), .BrUn(BrUn), .BrEq(BrEq), .BrLt(BrLt));
  // Probe on BrUn
  // Probe on ASel
  // Probe on BSel
  // Probe on ALUSel
  // Probe on MemWEn
  // Probe on WBSel
  partial_store partial_store_1 (
    .Instruction(Instruction_p), .MemAddress(MemAddress), .DataFromReg(ReadData2), .MemWEn(MemWEn),
    .MemWriteMask(MemWriteMask), .DataToMem(MemWriteData));
  partial_load partial_load_1 (
    .Instruction(Instruction_p), .MemAddress(MemAddress), .DataFromMem(MemReadData), .DataToReg(DataToReg));
  Multiplexer #(.select(2), .width(32)) multiplexer_5 (
    .in0(DataToReg), .in1(MemAddress), .in2(PCAdd4), .out(WBRegData), .sel(WBSel));  // open: in3

  // Other names for the same wires on the sheet: ALUResult[31:0] = MemAddress; WriteIndex[4:0] = Instruction_p[11:7];
  //   ReadIndex1[4:0] = Instruction_p[19:15]; ReadIndex2[4:0] = Instruction_p[24:20]

  // Notes on the sheet:
  //   To IMEM
  //   IMEM (do **NOT** move this)
  //   From IMEM
  //   Inputs/Outputs for testing. Do **NOT** move these.
  //   To DMEM
  //   DMEM (do **NOT** move this)
  //   From DMEM
endmodule
