// Logisim project partial-store.circ as structural Verilog: 1 circuit, main circuit partial_store
module partial_store (
  input  [31:0] Instruction,
  input  [31:0] MemAddress,
  input  [31:0] DataFromReg,
  input  MemWEn,
  output [3:0] MemWriteMask,
  output [31:0] DataToMem
);

  wire comparator_1_eq, comparator_2_eq, comparator_3_eq, comparator_4_eq;
  wire [2:0] OUTSel;
  wire [3:0] Mask_sb, Mask_sh;
  wire [31:0] Data2Mem_sb, Data2Mem_sh;

  // Probe on Instruction
  // Probe on MemAddress
  // Probe on DataFromReg
  // Probe on {{8{1'b0}}, DataFromReg[7:0], {16{1'b0}}}
  // Probe on {{16{1'b0}}, DataFromReg[7:0], {8{1'b0}}}
  // Probe on {{24{1'b0}}, DataFromReg[7:0]}
  // Probe on {DataFromReg[7:0], {24{1'b0}}}
  // Probe on {{16{1'b0}}, DataFromReg[15:0]}
  // Probe on {DataFromReg[15:0], {16{1'b0}}}
  Comparator #(.mode("unsigned"), .width(7)) comparator_1 (
    .a(Instruction[6:0]), .b(7'b0100011), .eq(comparator_1_eq));  // open: gt, lt
  Comparator #(.mode("unsigned"), .width(3)) comparator_2 (
    .a(Instruction[14:12]), .b(3'b000), .eq(comparator_2_eq));  // open: gt, lt
  Comparator #(.mode("unsigned"), .width(3)) comparator_3 (
    .a(Instruction[14:12]), .b(3'b001), .eq(comparator_3_eq));  // open: gt, lt
  Comparator #(.mode("unsigned"), .width(3)) comparator_4 (
    .a(Instruction[14:12]), .b(3'b010), .eq(comparator_4_eq));  // open: gt, lt
  Multiplexer #(.select(2), .width(4)) multiplexer_1 (
    .in0(4'b0001), .in1(4'b0010), .in2(4'b0100), .in3(4'b1000), .out(Mask_sb), .sel(MemAddress[1:0]));
  Multiplexer #(.select(2), .width(4)) multiplexer_2 (
    .in0(4'b0011), .in1(4'b0000), .in2(4'b1100), .in3(4'b0000), .out(Mask_sh), .sel(MemAddress[1:0]));
  Multiplexer #(.select(2), .width(32)) multiplexer_3 (
    .in0({{24{1'b0}}, DataFromReg[7:0]}), .in1({{16{1'b0}}, DataFromReg[7:0], {8{1'b0}}}),
    .in2({{8{1'b0}}, DataFromReg[7:0], {16{1'b0}}}), .in3({DataFromReg[7:0], {24{1'b0}}}), .out(Data2Mem_sb),
    .sel(MemAddress[1:0]));
  // Probe on MemAddress[1:0]
  Multiplexer #(.select(2), .width(32)) multiplexer_4 (
    .in0({{16{1'b0}}, DataFromReg[15:0]}), .in2({DataFromReg[15:0], {16{1'b0}}}), .out(Data2Mem_sh),
    .sel(MemAddress[1:0]));  // open: in1, in3
  and and_1 (OUTSel[0], comparator_1_eq, comparator_2_eq);
  and and_2 (OUTSel[1], comparator_1_eq, comparator_3_eq);
  and and_3 (OUTSel[2], comparator_1_eq, comparator_4_eq);
  // Probe on Data2Mem_sh
  // Probe on Data2Mem_sb
  // Probe on DataFromReg
  Multiplexer #(.select(3), .width(4)) multiplexer_5 (
    .in0(4'b0000), .in1(Mask_sb), .in2(Mask_sh), .in3(4'b0000), .in4(4'b1111), .in5(4'b0000), .in6(4'b0000),
    .in7(4'b0000), .out(MemWriteMask), .sel(OUTSel));
  Multiplexer #(.select(3), .width(32)) multiplexer_6 (
    .in1(Data2Mem_sb), .in2(Data2Mem_sh), .in4(DataFromReg), .out(DataToMem), .sel(OUTSel));  // open: in0, in3, in5, in6, in7
  // Probe on OUTSel
  // Probe on DataToMem

  // Other names for the same wires on the sheet: byte2[7:0] = DataFromReg[23:16]; byte23[15:0] = DataFromReg[31:16];
  //   Data2Mem_sw[31:0] = DataFromReg; byte3[7:0] = DataFromReg[31:24]; Opcode[6:0] = Instruction[6:0];
  //   Funct3[2:0] = Instruction[14:12]; Bottom2bits[1:0] = MemAddress[1:0]; sb = OUTSel[0]; sh = OUTSel[1];
  //   sw = OUTSel[2]; byte0[7:0] = DataFromReg[7:0]; byte01[15:0] = DataFromReg[15:0];
  //   pad_Byte0[7:0] = DataFromReg[7:0]; pad_Byte01[15:0] = DataFromReg[15:0]; pad_Byte1[15:8] = DataFromReg[7:0];
  //   pad_Byte2[23:16] = DataFromReg[7:0]; pad_Byte3[31:24] = DataFromReg[7:0]; pad_Byte23[31:16] = DataFromReg[15:0];
  //   byte1[7:0] = DataFromReg[15:8]

  // Notes on the sheet:
  //   INPUTS to your circuit
  //   DON'T CHANGE THE LOCATIONS OF THE INPUTS AND OUTPUTS!
  //   OUTPUT from your circuit
endmodule
