// Logisim project regfile.circ as structural Verilog: 1 circuit, main circuit regfile
module regfile (
  input  [4:0] ReadIndex1,
  input  [4:0] ReadIndex2,
  input  [4:0] WriteIndex,
  input  [31:0] WriteData,
  input  RegWEn,
  input  clk,
  output [31:0] ra,
  output [31:0] sp,
  output [31:0] t0,
  output [31:0] t1,
  output [31:0] t2,
  output [31:0] s0,
  output [31:0] s1,
  output [31:0] a0,
  output [31:0] ReadData1,
  output [31:0] ReadData2
);

  wire RegWEn_1, RegWEn_2, RegWEn_3, RegWEn_4, RegWEn_5, RegWEn_6, RegWEn_7, RegWEn_8, RegWEn_9, RegWEn_10,
       RegWEn_11, RegWEn_12, RegWEn_13, RegWEn_14, RegWEn_15, RegWEn_16, RegWEn_17, RegWEn_18, RegWEn_19,
       RegWEn_20, RegWEn_21, RegWEn_22, RegWEn_23, RegWEn_24, RegWEn_25, RegWEn_26, RegWEn_27, RegWEn_28,
       RegWEn_29, RegWEn_30, RegWEn_31;
  wire [31:0] X3, X4, X11, X12, X13, X14, X15, X16, X17, X18, X19, X20, X21, X22, X23, X24, X25, X26, X27,
       X28, X29, X30, X31;

  Register #(.width(32)) register_1 (.D(WriteData), .en(RegWEn_8), .clk(clk), .Q(s0));  // open: clr
  Register #(.width(32)) register_2 (.D(WriteData), .en(RegWEn_16), .clk(clk), .Q(X16));  // open: clr
  Register #(.width(32)) register_3 (.D(WriteData), .en(RegWEn_24), .clk(clk), .Q(X24));  // open: clr
  Register #(.width(32)) register_4 (.D(WriteData), .en(RegWEn_1), .clk(clk), .Q(ra));  // open: clr
  Register #(.width(32)) register_5 (.D(WriteData), .en(RegWEn_9), .clk(clk), .Q(s1));  // open: clr
  Register #(.width(32)) register_6 (.D(WriteData), .en(RegWEn_17), .clk(clk), .Q(X17));  // open: clr
  Register #(.width(32)) register_7 (.D(WriteData), .en(RegWEn_25), .clk(clk), .Q(X25));  // open: clr
  Multiplexer #(.select(5), .width(32)) multiplexer_1 (
    .in0({32{1'b0}}), .in1(ra), .in2(sp), .in3(X3), .in4(X4), .in5(t0), .in6(t1), .in7(t2), .in8(s0),
    .in9(s1), .in10(a0), .in11(X11), .in12(X12), .in13(X13), .in14(X14), .in15(X15), .in16(X16), .in17(X17),
    .in18(X18), .in19(X19), .in20(X20), .in21(X21), .in22(X22), .in23(X23), .in24(X24), .in25(X25),
    .in26(X26), .in27(X27), .in28(X28), .in29(X29), .in30(X30), .in31(X31), .out(ReadData1), .sel(ReadIndex1));
  Register #(.width(32)) register_8 (.D(WriteData), .en(RegWEn_2), .clk(clk), .Q(sp));  // open: clr
  Register #(.width(32)) register_9 (.D(WriteData), .en(RegWEn_10), .clk(clk), .Q(a0));  // open: clr
  Register #(.width(32)) register_10 (.D(WriteData), .en(RegWEn_18), .clk(clk), .Q(X18));  // open: clr
  Register #(.width(32)) register_11 (.D(WriteData), .en(RegWEn_26), .clk(clk), .Q(X26));  // open: clr
  Register #(.width(32)) register_12 (.D(WriteData), .en(RegWEn_3), .clk(clk), .Q(X3));  // open: clr
  Register #(.width(32)) register_13 (.D(WriteData), .en(RegWEn_11), .clk(clk), .Q(X11));  // open: clr
  Register #(.width(32)) register_14 (.D(WriteData), .en(RegWEn_19), .clk(clk), .Q(X19));  // open: clr
  Register #(.width(32)) register_15 (.D(WriteData), .en(RegWEn_27), .clk(clk), .Q(X27));  // open: clr
  Multiplexer #(.select(5), .width(32)) multiplexer_2 (
    .in0({32{1'b0}}), .in1(ra), .in2(sp), .in3(X3), .in4(X4), .in5(t0), .in6(t1), .in7(t2), .in8(s0),
    .in9(s1), .in10(a0), .in11(X11), .in12(X12), .in13(X13), .in14(X14), .in15(X15), .in16(X16), .in17(X17),
    .in18(X18), .in19(X19), .in20(X20), .in21(X21), .in22(X22), .in23(X23), .in24(X24), .in25(X25),
    .in26(X26), .in27(X27), .in28(X28), .in29(X29), .in30(X30), .in31(X31), .out(ReadData2), .sel(ReadIndex2));
  Register #(.width(32)) register_16 (.D(WriteData), .en(RegWEn_4), .clk(clk), .Q(X4));  // open: clr
  Register #(.width(32)) register_17 (.D(WriteData), .en(RegWEn_12), .clk(clk), .Q(X12));  // open: clr
  Register #(.width(32)) register_18 (.D(WriteData), .en(RegWEn_20), .clk(clk), .Q(X20));  // open: clr
  Register #(.width(32)) register_19 (.D(WriteData), .en(RegWEn_28), .clk(clk), .Q(X28));  // open: clr
  Register #(.width(32)) register_20 (.D(WriteData), .en(RegWEn_5), .clk(clk), .Q(t0));  // open: clr
  Register #(.width(32)) register_21 (.D(WriteData), .en(RegWEn_13), .clk(clk), .Q(X13));  // open: clr
  Register #(.width(32)) register_22 (.D(WriteData), .en(RegWEn_21), .clk(clk), .Q(X21));  // open: clr
  Register #(.width(32)) register_23 (.D(WriteData), .en(RegWEn_29), .clk(clk), .Q(X29));  // open: clr
  Register #(.width(32)) register_24 (.D(WriteData), .en(RegWEn_6), .clk(clk), .Q(t1));  // open: clr
  Register #(.width(32)) register_25 (.D(WriteData), .en(RegWEn_14), .clk(clk), .Q(X14));  // open: clr
  Register #(.width(32)) register_26 (.D(WriteData), .en(RegWEn_22), .clk(clk), .Q(X22));  // open: clr
  Register #(.width(32)) register_27 (.D(WriteData), .en(RegWEn_30), .clk(clk), .Q(X30));  // open: clr
  Register #(.width(32)) register_28 (.D(WriteData), .en(RegWEn_7), .clk(clk), .Q(t2));  // open: clr
  Register #(.width(32)) register_29 (.D(WriteData), .en(RegWEn_15), .clk(clk), .Q(X15));  // open: clr
  Register #(.width(32)) register_30 (.D(WriteData), .en(RegWEn_23), .clk(clk), .Q(X23));  // open: clr
  Register #(.width(32)) register_31 (.D(WriteData), .en(RegWEn_31), .clk(clk), .Q(X31));  // open: clr
  Demultiplexer #(.select(5)) demultiplexer_1 (
    .out1(RegWEn_1), .out2(RegWEn_2), .out3(RegWEn_3), .out4(RegWEn_4), .out5(RegWEn_5), .out6(RegWEn_6),
    .out7(RegWEn_7), .out8(RegWEn_8), .out9(RegWEn_9), .out10(RegWEn_10), .out11(RegWEn_11),
    .out12(RegWEn_12), .out13(RegWEn_13), .out14(RegWEn_14), .out15(RegWEn_15), .out16(RegWEn_16),
    .out17(RegWEn_17), .out18(RegWEn_18), .out19(RegWEn_19), .out20(RegWEn_20), .out21(RegWEn_21),
    .out22(RegWEn_22), .out23(RegWEn_23), .out24(RegWEn_24), .out25(RegWEn_25), .out26(RegWEn_26),
    .out27(RegWEn_27), .out28(RegWEn_28), .out29(RegWEn_29), .out30(RegWEn_30), .out31(RegWEn_31),
    .in(RegWEn), .sel(WriteIndex));  // open: out0

  // Other names for the same wires on the sheet: X1[31:0] = ra; X2[31:0] = sp; X5[31:0] = t0; X6[31:0] = t1;
  //   X7[31:0] = t2; X8[31:0] = s0; X9[31:0] = s1; X10[31:0] = a0

  // Notes on the sheet:
  //   INPUTS to your circuit
  //   DON'T CHANGE THE LOCATIONS OF THE INPUTS AND OUTPUTS!
  //   These are DEBUG/TEST outputs from your circuit.
  //   OUTPUTS from your circuit
endmodule
