// Logisim project I-type-random-test-100.circ as structural Verilog: 1 circuit, main circuit run_main
module run_main (
  output [31:0] ra,
  output [31:0] sp,
  output [31:0] t0,
  output [31:0] t1,
  output [31:0] t2,
  output [31:0] s0,
  output [31:0] s1,
  output [31:0] a0,
  output [31:0] RequestedAddress,
  output [31:0] RequestedInstruction,
  output [15:0] TimeStep,
  output halt
);

  wire clk;

  Clock clock_1 (.out(clk));
  // Probe on RequestedAddress
  // cpu_harness cpu_harness_1: pin names not known; wires that end beside it: RequestedInstruction, clk, RequestedAddress, ra, sp, t0, t1, t2, s0, s1, a0
  ROM #(.addrWidth(14), .dataWidth(32)) rom_1 (.addr(RequestedAddress[15:2]), .data(RequestedInstruction));
  // Probe on RequestedInstruction
  Counter #(.max('hffff), .width(16)) counter_1 (.clk(clk), .Q(TimeStep));  // open: clr, load, up, count, D, carry
  Comparator #(.width(16)) comparator_1 (.a(TimeStep), .b(16'h66), .eq(halt));  // open: gt, lt

  // Other names for the same wires on the sheet: Instruction[31:0] = RequestedInstruction;
  //   ProgramCounter[31:0] = RequestedAddress

  // Notes on the sheet:
  //   contents of rom_1 (hex, n*v repeats v):
  //   a37293 930293 56513 fe540093 b08293 ff516413 ff43a293 ff456493 1438393 60f113 1b51113 1435093
  //   1529393 4123d113 fe92e113 1e30113 b2c513 ff732093 1108093 133e393 1249113 fe356093 1132513 d09313
  //   112f293 ff256393 40d35313 535393 ff730293 ff540113 122f113 649113 ffc40493 1b47393 41445513 1529413
  //   ffa37113 1b08093 feb10413 fea4f093 fe612093 74e113 1840513 336093 242093 fee50393 fef2e293 1137413
  //   1755393 103a493 b0f093 4d513 548513 4094d313 ffe12413 4053d293 1441413 e37393 40c35313 ffa28313
  //   ffc17293 4113d513 4060d293 ffc56513 1e3f413 ff80e313 22a393 ffc38493 4122d513 fef4e093 93e393
  //   41d3d493 41955113 1839493 646293 fe044393 e48113 1735093 ff332093 849093 509513 a11393 172c313
  //   40d3d113 1d36313 ff12a293 e31313 ff746093 41245393 829393 ffc3e493 40f313 ffb3e313 f16113 41e45093
  //   e35313 fff44513 fef44313 fec0c493 1a51513
  //   Instruction Memory
  //   Halts Execution After Constant # of Clock Cycles
  //   Constant
endmodule
