// Logisim project I-type-random-test-1000.circ as structural Verilog: 1 circuit, main circuit run_main
module run_main (
  output [31:0] ra,
  output [31:0] sp,
  output [31:0] t0,
  output [31:0] t1,
  output [31:0] t2,
  output [31:0] s0,
  output [31:0] s1,
  output [31:0] a0,
  output [31:0] RequestedAddress,
  output [31:0] RequestedInstruction,
  output [15:0] TimeStep,
  output halt
);

  wire clk;

  Clock clock_1 (.out(clk));
  // Probe on RequestedAddress
  // cpu_harness cpu_harness_1: pin names not known; wires that end beside it: RequestedInstruction, clk, RequestedAddress, ra, sp, t0, t1, t2, s0, s1, a0
  ROM #(.addrWidth(14), .dataWidth(32)) rom_1 (.addr(RequestedAddress[15:2]), .data(RequestedInstruction));
  // Probe on RequestedInstruction
  Counter #(.max('hffff), .width(16)) counter_1 (.clk(clk), .Q(TimeStep));  // open: clr, load, up, count, D, carry
  Comparator #(.width(16)) comparator_1 (.a(TimeStep), .b(16'h3ea), .eq(halt));  // open: gt, lt

  // Other names for the same wires on the sheet: Instruction[31:0] = RequestedInstruction;
  //   ProgramCounter[31:0] = RequestedAddress

  // Notes on the sheet:
  //   contents of rom_1 (hex, n*v repeats v):
  //   8e657293 b53f393 9f710413 bfb46093 af012293 909313 5214e313 34152093 a2438313 145293 1e49413 1b45513
  //   a7530093 4170d493 26c0a393 7b548393 8944a093 81d4f313 49054393 98756113 849113 e11413 7e94c413
  //   41a3d393 9a830113 4f04e293 40115393 7cf34393 1655413 f193a493 3642e493 103d413 bc728393 1431413
  //   8c84e293 98417313 c39293 7e73a413 449093 aad2c293 2b28413 29e50393 de737513 37612113 9c43f413
  //   4162d413 441413 18712293 1a3d313 4b248293 69c47093 8180a313 72d413 30948393 a4f54513 c9908493
  //   8a64a393 d242f393 41745493 1637393 4190d413 40a3d493 1523e393 a45313 a0d513 be248413 40835313
  //   d5a48313 4640c493 46e38313 75c36093 28a4e493 3fc08093 ad634413 d4957493 b2a28313 7f146113 89657113
  //   40a35093 609293 f3a32113 82632093 a574f113 40840293 dfb0a413 b45393 fec12293 1241413 40135093 539093
  //   4080d293 645413 4064d413 1bd40093 4c016113 8c22f293 1be4e113 e3f4c113 72110393 d6e12313 1239493
  //   7060c113 2663a513 35854513 5f40093 b6b17413 f11413 e7150393 c49293 b2944493 67544413 209393 c4c3e513
  //   1262e493 1aa56413 41c35113 47732113 1411493 4ca14293 ac28113 22a56113 77647313 32838393 183a493
  //   1251413 75d32313 d7642393 1f45393 c4140293 e1030293 1229493 95356393 4f940493 a04c393 cfa16113
  //   1535293 715393 c4d393 10d2a293 34852313 ad740113 1e55093 6f20f393 67b32493 41155293 eb042093
  //   a663c393 9360c413 8732113 4150d093 e9934293 ab70c493 95914293 40435393 611093 829093 40b4d093 211293
  //   73257313 61a36493 4134d393 98b10293 4012d093 cff4a113 e11513 3394a113 b3634493 f6b57293 b29113
  //   42546113 3be37493 739393 629313 41e3f293 95a10393 d4d513 dec4c393 2ba42513 40a2d113 9bc42113
  //   40755113 69544093 651393 183d093 4383c313 1d35413 25447093 68057513 9bd46113 71f3e313 8ad44093
  //   b29293 1229113 4142d513 1982a393 72d313 2ee52093 1b45393 c0d513 339393 e8237393 6d62a493 53f42313
  //   4644a513 1929313 2a10393 9542f513 2aa46413 f41513 1809313 52f52493 4eb2f293 311093 d3d293 6f00c293
  //   1d2d293 aad2a413 ede4f093 a39093 ded36413 b6840413 f790f413 ac73c093 9b308313 84d393 fb946393
  //   41935293 4110d493 1b3d513 183d093 241413 1441393 13f3e113 76157493 4f63e313 40435113 4072d093
  //   e8447513 1f39493 39754113 adf34513 351513 5aa52513 b2c3c413 75a56513 df32f313 5d248093 ee917493
  //   e4d413 41930513 cd83a093 d5210513 f2d093 5b30a513 845093 5520a493 89148113 1d39393 71f4e113 4024d093
  //   f942f493 5553a113 509293 41055413 151093 c5b4f393 b3630393 4162d393 ee308113 15837113 ab32f293
  //   64c2e493 1a15313 4d717093 eff2e413 1f2d513 adb2f313 945113 fc942293 41e15413 6e008393 d7044093
  //   23756293 c904f093 ef62e093 9b436493 d4136393 132d513 c6e40093 d6e4a313 f4d493 beb0e393 d2e2c113
  //   1539513 4003d413 4f547513 4173d493 bdf0e093 bc50a413 ac216413 9dc42393 1360a293 d480e113 bc34a293
  //   26c34493 80d093 40735293 afd50293 d8f28113 6b2f113 40c45293 1809513 4094d513 f6c0a093 b0b34113
  //   67554413 40f4d313 239393 a9f2f293 21d16113 239313 64a10513 12d093 41035293 74238093 d7c42393
  //   12450313 4c134413 8200c493 e55093 b7b3e393 8b13c393 91f46093 4113d413 33c4f413 14d413 7a042393
  //   80a40113 b122f093 4df32113 62d28393 41e45313 81a56513 645093 79a2e113 41645393 8c33f093 32756113
  //   97146093 d41413 92737493 4b62f293 b830f313 180d093 1b31093 1b4d493 7e72e093 a7f44093 24647313 60d413
  //   e610f413 1af0f393 9ed4a413 13c36313 c630313 41f2d413 62750493 41235493 8e63f513 1d834513 4dd2f113
  //   4124d393 d45413 fd930513 849293 f952f493 da94e313 12d413 9552293 14948493 409313 4020a393 b31493
  //   d31313 23a28313 1335313 35308393 d7917093 80332113 a0c08513 41455513 211093 41345093 1945413
  //   41c4d093 47840413 1615313 41735093 1909513 46540293 40d3d113 951413 4133d413 1235093 955493 79254393
  //   41737093 4172d313 4a528493 2a628393 87f0f493 1b49113 bbb40293 a55413 41d15313 60e47293 9bd0a513
  //   64e37313 1632293 cf62a513 c43a413 1e538413 18130393 1249513 65236093 7ad46413 58536493 57e36513
  //   1422a493 1c2d493 c4d113 41235293 100d313 3fd37393 4193d093 e480a313 6d217293 40b45093 8552e493
  //   d7032493 4f808393 31517513 66247093 a7d48293 25936293 4074d113 61512293 40715293 60c14413 1ee40413
  //   a642f113 6510f093 6920c393 451313 3c23c513 ab834413 3553f413 149113 cb850113 539493 d9e36493
  //   f6d32393 f7436313 45732393 4140d493 46748413 1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
  //   Instruction Memory
  //   Halts Execution After Constant # of Clock Cycles
  //   Constant
endmodule
